# Fritzing sketch Diagrama_Competicao (saved by Fritzing 0.9.3b)
breadboards: 3

parts:
  Mod2 = gy-906  # not connected
  M1 = LJ18A3-H-ZBX [package=THT]  # not connected
  Mod3 = ossoyoo-lora-module
  M2 = LJ18A3-H-ZBX [package=THT]  # not connected
  M3 = LJ18A3-H-ZBX [package=THT]  # not connected
  MH-ET_LIVE_ESP32_DEVKIT1 = MH-ET LIVE ESP32 DEVKIT 38 pins
  Componente1 = LCD1602-I2C
  Componente2 = JeePlug experimenter's board
  U1 = LM2596 step down module
  BATT1 = LiPoly Battery (1300mAh)
  U2 = Optocoupler [package=THT]
  R2 = Temperature Sensor (Thermistor) [thermistor_type=NTC package=THT]
  R3 = Temperature Sensor (Thermistor) [thermistor_type=NTC package=THT]
  R4 = Temperature Sensor (Thermistor) [thermistor_type=NTC package=THT]
  R5 = Resistor [tolerance=±5% resistance=220 package="2512 [SMD]"]
  R6 = Resistor [tolerance=±5% resistance=220 package="2512 [SMD]"]
  R7 = Resistor [tolerance=±5% resistance=220 package="2512 [SMD]"]
  R8 = Resistor [tolerance=±5% resistance=220 package="2512 [SMD]"]
  R9 = Temperature Sensor (Thermistor) [thermistor_type=NTC package=THT]

nets:
  N1: Mod3.M0, Mod3.M1, Mod3.GND, MH-ET_LIVE_ESP32_DEVKIT1.GND#64, U1.IN-, U1.OUT-, BATT1.negative
  N2: Mod3.RXD, MH-ET_LIVE_ESP32_DEVKIT1.IO16
  N3: Mod3.TXD, MH-ET_LIVE_ESP32_DEVKIT1.IO17
  VCC: Mod3.VCC, MH-ET_LIVE_ESP32_DEVKIT1.3V3, Componente1.VCC
  N4: MH-ET_LIVE_ESP32_DEVKIT1.IO26, R8.Pin_0, R9.pin_0
  N5: MH-ET_LIVE_ESP32_DEVKIT1.IO27, R3.pin_0, R7.Pin_0
  N6: MH-ET_LIVE_ESP32_DEVKIT1.IO14, R2.pin_0, R6.Pin_0
  N7: MH-ET_LIVE_ESP32_DEVKIT1.IO12, R4.pin_0, R5.Pin_0
  N8: MH-ET_LIVE_ESP32_DEVKIT1.GND#58, R5.Pin_1, R6.Pin_1, R7.Pin_1, R8.Pin_1
  N9: MH-ET_LIVE_ESP32_DEVKIT1.5V, U1.OUT+
  N10: Componente2.N$17, U2.Pin_1
  N11: Componente2.N$18, U2.Pin_2
  N12: Componente2.N$19, U2.Pin_3
  N13: Componente2.N$41, U2.Pin_6
  N14: Componente2.N$42, U2.Pin_5
  N15: Componente2.N$43, U2.Pin_4
  N16: U1.IN+, BATT1.positive
  N17: R2.pin_1, R3.pin_1, R4.pin_1, R9.pin_1

custom parts:
  gy-906: gy-906 Non-contact PIR I2C interface temperature sensor breakout board.
  LJ18A3-H-ZBX: LJ18A3-H-ZBX Proximity Sensor module.
  ossoyoo-lora-module: Osoyoo Long Distance wireless transceiver Uart LoRa Module.
  MH-ET LIVE ESP32 DEVKIT 38 pins: http://mh.nodebb.com/topic/2/mh-et-live-esp32-devkit
  LCD1602-I2C: A standard character display, usually with 2x16 characters. Comes in many colors with LCM1602 IIC attached.
  LM2596 step down module: LM2596 DC-DC step down power supply module 3 A.
  LiPoly Battery (1300mAh): Lithium Ion Polymer Battery (1300mAh)
